# Fritzing sketch Sketch (saved by Fritzing 0.4.3b)
breadboards: 1

parts:
  Arduino1 = Arduino
  LED1 = Blue LED - 5mm
  LED2 = Red LED - 5mm
  LED1_2 = Blue LED - 5mm
  LED3 = yellow LED - 5mm
  LED4 = white LED - 5mm
  LED5 = green LED - 5mm
  R1 = Resistor [resistance=220 package=THT]
  R1_2 = Resistor [resistance=220 package=THT]
  R1_3 = Resistor [resistance=220 package=THT]
  R1_4 = Resistor [resistance=220 package=THT]
  R1_5 = Resistor [resistance=220 package=THT]
  S1 = Pushbutton [package=THT]
  R3 = Resistor [resistance=220 package=THT]

nets:
  N1: Arduino1.GND, R1.Pin_0, R1_2.Pin_0, R1_3.Pin_0, R1_4.Pin_0, R1_5.Pin_0, R3.Pin_0
  N2: Arduino1.D13, LED1.anode, LED1_2.anode
  N3: Arduino1.D12, LED2.anode
  N4: Arduino1.D9, LED3.anode
  N5: Arduino1.D8, S1.leg1, R3.Pin_1
  N6: Arduino1.D7, LED4.anode
  N7: Arduino1.D4, LED5.anode
  N8: Arduino1.+5V, S1.leg0
  N9: LED1.cathode, LED1_2.cathode, R1.Pin_1
  N10: LED2.cathode, R1_2.Pin_1
  N11: LED3.cathode, R1_3.Pin_1
  N12: LED4.cathode, R1_4.Pin_1
  N13: LED5.cathode, R1_5.Pin_1
