# Fritzing sketch 8SegLED (saved by Fritzing 0.4.3b)
breadboards: 1

parts:
  DI1 = 7-Segment LED Display [package=THT]
  Arduino1 = Arduino

nets:
  N1: DI1.cathodeE, Arduino1.D6
  N2: DI1.cathodeD, Arduino1.D5
  N3: DI1.commAnode#2, Arduino1.D4
  N4: DI1.cathodeC, Arduino1.D3
  N5: DI1.cathodeDP, Arduino1.D2
  N6: DI1.cathodeB, Arduino1.D7
  N7: DI1.cathodeA, Arduino1.D11
  N8: DI1.cathodeF, Arduino1.D12
  N9: DI1.cathodeG, Arduino1.D13
